# Fritzing sketch Ingition Injector 6 Sequancial Modul (saved by Fritzing 0.9.3b)
circuit board: 5cm x 4cm
breadboards: 1

parts:
  JP1 = female pin header, 3 pins [form="♀ (female)"]
  R62 = Resistor [tolerance=±5% resistance=100k package=THT]
  R66 = Resistor [tolerance=±5% resistance=100k package=THT]
  IC5 = IC, DIP package, 8 pins [chip_label=IC part_number=TC4424EPA]
  R59 = Resistor [tolerance=±5% resistance=1k package=THT]
  R63 = Resistor [tolerance=±5% resistance=1k package=THT]
  C24 = Ceramic Capacitor [capacitance=1µF package="200 mil [THT, multilayer]"]
  R60 = Resistor [tolerance=±5% resistance=160 power=2W package=THT]
  R64 = Resistor [tolerance=±5% resistance=160 power=2W package=THT]
  R61 = Resistor [tolerance=±5% resistance=2.4k package=THT]
  R65 = Resistor [tolerance=±5% resistance=2.4k package=THT]
  R70 = Resistor [tolerance=±5% resistance=680 package=THT]
  R67 = Resistor [tolerance=±5% resistance=680 package=THT]
  LED12 = LED - 3mm [color="Red (633nm)" package="3 mm [THT]"]
  LED11 = LED - 3mm [color="Red (633nm)" package="3 mm [THT]"]
  D18 = Rectifier Diode [part_number=1N4004 package="300 mil [THT]"]
  D17 = Rectifier Diode [part_number=1N4004 package="300 mil [THT]"]
  Q10 = Basic FET N-Channel [part_number=STP62NS04Z package="TO220 [THT]"]
  Q9 = Basic FET N-Channel [part_number=STP62NS04Z package="TO220 [THT]"]
  R71 = Resistor [tolerance=±5% resistance=1k package=THT]
  R68 = Resistor [tolerance=±5% resistance=1k package=THT]
  R72 = Resistor [tolerance=±5% resistance=100k package=THT]
  R69 = Resistor [tolerance=±5% resistance=100k package=THT]
  LED9 = LED - 3mm [color="Red (633nm)" package="3 mm [THT]"]
  LED10 = LED - 3mm [color="Red (633nm)" package="3 mm [THT]"]
  J5_5v-12v = screw terminal, 2 pins
  IGN-5/6-OUT = screw terminal, 2 pins
  INJ-5/6-OUT = screw terminal, 2 pins
  IGN-5-IN = female pin header, 1 pin [form="♀ (female)"]
  IGN-6-IN = female pin header, 1 pin [form="♀ (female)"]
  INJ-5-IN = female pin header, 1 pin [form="♀ (female)"]
  INJ-6-IN = female pin header, 1 pin [form="♀ (female)"]

nets:
  5V: JP1.pin1, J5_5v-12v.pin2
  JP1-OUT: JP1.pin2, IC5.pin6, C24.1
  12V: JP1.pin3, R70.Pin_0, R67.Pin_0, J5_5v-12v.pin1
  GND: R62.Pin_0, R66.Pin_0, IC5.pin3, C24.0, Q10.source, Q9.source, R72.Pin_1, R69.Pin_1, LED9.cathode, LED10.cathode
  N1: R62.Pin_1, IC5.pin2, R59.Pin_1
  N2: R66.Pin_1, IC5.pin4, R63.Pin_1
  N3: IC5.pin5, R64.Pin_0
  N4: IC5.pin7, R60.Pin_1
  IGN5-CPU-D??: R59.Pin_0, IGN-5-IN.pin1
  IGN6-CPU-D??: R63.Pin_0, IGN-6-IN.pin1
  IGN-5-OUT: R60.Pin_0, R61.Pin_1, IGN-5/6-OUT.pin2
  IGN-6-OUT: R64.Pin_1, R65.Pin_1, IGN-5/6-OUT.pin1
  N5: R61.Pin_0, LED9.anode
  N6: R65.Pin_0, LED10.anode
  N7: R70.Pin_1, LED12.anode
  N8: R67.Pin_1, LED11.anode
  N9: LED12.cathode, D18.anode
  N10: LED11.cathode, D17.anode
  INJ-6-OUT: D18.cathode, Q10.drain, INJ-5/6-OUT.pin1
  INJ-5-OUT: D17.cathode, Q9.drain, INJ-5/6-OUT.pin2
  N11: Q10.gate, R71.Pin_1
  N12: Q9.gate, R68.Pin_1
  INJ6-CPU-D??: R71.Pin_0, R72.Pin_0, INJ-6-IN.pin1
  INJ5-CPU-D??: R68.Pin_0, R69.Pin_0, INJ-5-IN.pin1

notes:
  Ignitor output 3
  Injector 6
  Injector 5
