# Fritzing sketch Ingition Injector 5-6 Sequancial Modul Rev.0.1 (saved by Fritzing 0.9.3b)
circuit board: 3.19768cm x 3.45853cm
breadboards: 1

parts:
  R62 = Resistor [tolerance=±5% resistance=100k package=THT]
  R66 = Resistor [tolerance=±5% resistance=100k package=THT]
  R59 = Resistor [tolerance=±5% resistance=1k package=THT]
  R63 = Resistor [tolerance=±5% resistance=1k package=THT]
  C24 = Ceramic Capacitor [capacitance=1µF package="200 mil [THT, multilayer]"]
  R60 = Resistor [tolerance=±5% resistance=160 power=2W package=THT]
  R64 = Resistor [tolerance=±5% resistance=160 power=2W package=THT]
  R61 = Resistor [tolerance=±5% resistance=2.4k package=THT]
  R65 = Resistor [tolerance=±5% resistance=2.4k package=THT]
  R70 = Resistor [tolerance=±5% resistance=680 package=THT]
  R67 = Resistor [tolerance=±5% resistance=680 package=THT]
  LED12 = LED - 3mm [color="Red (633nm)" package="3 mm [THT]"]
  LED11 = LED - 3mm [color="Red (633nm)" package="3 mm [THT]"]
  D18 = Rectifier Diode [part_number=1N4004 package="300 mil [THT]"]
  D17 = Rectifier Diode [part_number=1N4004 package="300 mil [THT]"]
  Q10 = Basic FET N-Channel [part_number=STP62NS04Z package="TO220 [THT]"]
  Q9 = Basic FET N-Channel [part_number=STP62NS04Z package="TO220 [THT]"]
  R71 = Resistor [tolerance=±5% resistance=1k package=THT]
  R68 = Resistor [tolerance=±5% resistance=1k package=THT]
  R72 = Resistor [tolerance=±5% resistance=100k package=THT]
  R69 = Resistor [tolerance=±5% resistance=100k package=THT]
  LED10 = LED - 3mm [color="Red (633nm)" package="3 mm [THT]"]
  IGN-5/6-OUT = screw terminal, 2 pins
  INJ-5/6-OUT = screw terminal, 2 pins
  IGN5IN = female pin header, 1 pin [form="♀ (female)"]
  IGN6IN = female pin header, 1 pin [form="♀ (female)"]
  INJ5IN = female pin header, 1 pin [form="♀ (female)"]
  INJ6IN = female pin header, 1 pin [form="♀ (female)"]
  LED9 = LED - 3mm [color="Red (633nm)" package="3 mm [THT]"]
  IC5 = IC, DIP package, 8 pins [chip_label=IC part_number=TC4424EPA]
  5v/12V = Pad [width=3 height=5 connect=center]
  GND = Pad [width=3 height=5 connect=center]  # not connected

nets:
  GND: R62.Pin_0, R66.Pin_0, C24.0, Q10.source, Q9.source, R72.Pin_1, R69.Pin_1, LED10.cathode, LED9.cathode, IC5.pin3
  N1: R62.Pin_1, R59.Pin_1, IC5.pin2
  N2: R66.Pin_1, R63.Pin_1, IC5.pin4
  IGN5-CPU-D??: R59.Pin_0, IGN5IN.pin1
  IGN6-CPU-D??: R63.Pin_0, IGN6IN.pin1
  N3: C24.1, IC5.pin6, 5v/12V.pad
  IGN-5-OUT: R60.Pin_0, R61.Pin_1, IGN-5/6-OUT.pin2
  N4: R60.Pin_1, IC5.pin7
  N5: R64.Pin_0, IC5.pin5
  IGN-6-OUT: R64.Pin_1, R65.Pin_1, IGN-5/6-OUT.pin1
  N6: R61.Pin_0, LED9.anode
  N7: R65.Pin_0, LED10.anode
  12V: R70.Pin_0, R67.Pin_0
  N8: R70.Pin_1, LED12.anode
  N9: R67.Pin_1, LED11.anode
  N10: LED12.cathode, D18.anode
  N11: LED11.cathode, D17.anode
  INJ-6-OUT: D18.cathode, Q10.drain, INJ-5/6-OUT.pin1
  INJ-5-OUT: D17.cathode, Q9.drain, INJ-5/6-OUT.pin2
  N12: Q10.gate, R71.Pin_1
  N13: Q9.gate, R68.Pin_1
  INJ6-CPU-D??: R71.Pin_0, R72.Pin_0, INJ6IN.pin1
  INJ5-CPU-D??: R68.Pin_0, R69.Pin_0, INJ5IN.pin1

notes:
  Ignitor output 3
  Injector 6
  Injector 5
  AmesisProject Full 5/6 Rev 0.1
  GND
  5v/12v
  ING5
  ING6
  INJ5
  INJ6
