# Fritzing sketch Ingition Injector 8 Sequancial Modul (saved by Fritzing 0.9.3b)
circuit board: 5.1cm x 5.3cm
breadboards: 1

parts:
  C25 = Ceramic Capacitor [capacitance=1µF package="200 mil [THT, multilayer]"]
  IC6 = IC, DIP package, 8 pins [chip_label=IC part_number=TC4424EPA]
  R63 = Resistor [tolerance=±5% resistance=1k package=THT]
  R62 = Resistor [tolerance=±5% resistance=100k package=THT]
  R84 = Resistor [tolerance=±5% resistance=680 package=THT]
  Q10 = Basic FET N-Channel [part_number=STP62NS04Z package="TO220 [THT]"]
  LED16 = LED - 3mm [color="Red (633nm)" package="3 mm [THT]"]
  R72 = Resistor [tolerance=±5% resistance=100k package=THT]
  R76 = Resistor [tolerance=±5% resistance=100k package=THT]
  Q9 = Basic FET N-Channel [part_number=STP62NS04Z package="TO220 [THT]"]
  IC5 = IC, DIP package, 8 pins [chip_label=IC part_number=TC4424EPA]
  LED11 = LED - 3mm [color="Red (633nm)" package="3 mm [THT]"]
  D20 = Rectifier Diode [part_number=1N4004 package="300 mil [THT]"]
  R77 = Resistor [tolerance=±5% resistance=1k package=THT]
  R67 = Resistor [tolerance=±5% resistance=680 package=THT]
  LED15 = LED - 3mm [color="Red (633nm)" package="3 mm [THT]"]
  LED9 = LED - 3mm [color="Red (633nm)" package="3 mm [THT]"]
  R60 = Resistor [tolerance=±5% resistance=160 power=2W package=THT]
  R70 = Resistor [tolerance=±5% resistance=680 package=THT]
  Q11 = Basic FET N-Channel [part_number=STP62NS04Z package="TO220 [THT]"]
  R59 = Resistor [tolerance=±5% resistance=1k package=THT]
  R71 = Resistor [tolerance=±5% resistance=1k package=THT]
  R65 = Resistor [tolerance=±5% resistance=2.4k package=THT]
  R64 = Resistor [tolerance=±5% resistance=160 power=2W package=THT]
  C24 = Ceramic Capacitor [capacitance=1µF package="200 mil [THT, multilayer]"]
  R73 = Resistor [tolerance=±5% resistance=1k package=THT]
  R82 = Resistor [tolerance=±5% resistance=1k package=THT]
  D19 = Rectifier Diode [part_number=1N4004 package="300 mil [THT]"]
  LED13 = LED - 3mm [color="Red (633nm)" package="3 mm [THT]"]
  R83 = Resistor [tolerance=±5% resistance=100k package=THT]
  R61 = Resistor [tolerance=±5% resistance=2.4k package=THT]
  INJ-IN = female pin header, 4 pins [form="♀ (female)"]
  R86 = Resistor [tolerance=±5% resistance=100k package=THT]
  LED12 = LED - 3mm [color="Red (633nm)" package="3 mm [THT]"]
  Q12 = Basic FET N-Channel [part_number=STP62NS04Z package="TO220 [THT]"]
  ING-7/8-OUT = screw terminal, 2 pins
  R79 = Resistor [tolerance=±5% resistance=2.4k package=THT]
  R81 = Resistor [tolerance=±5% resistance=680 package=THT]
  R69 = Resistor [tolerance=±5% resistance=100k package=THT]
  R80 = Resistor [tolerance=±5% resistance=100k package=THT]
  R74 = Resistor [tolerance=±5% resistance=160 power=2W package=THT]
  LED14 = LED - 3mm [color="Red (633nm)" package="3 mm [THT]"]
  R85 = Resistor [tolerance=±5% resistance=1k package=THT]
  ING-5/6-OUT = screw terminal, 2 pins
  R78 = Resistor [tolerance=±5% resistance=160 power=2W package=THT]
  R66 = Resistor [tolerance=±5% resistance=100k package=THT]
  ING-IN = female pin header, 4 pins [form="♀ (female)"]
  GND-5/12v = screw terminal, 2 pins
  INJ-7/8-OUT = screw terminal, 2 pins
  R68 = Resistor [tolerance=±5% resistance=1k package=THT]
  D17 = Rectifier Diode [part_number=1N4004 package="300 mil [THT]"]
  R75 = Resistor [tolerance=±5% resistance=2.4k package=THT]
  D18 = Rectifier Diode [part_number=1N4004 package="300 mil [THT]"]
  INJ-5/6-OUT = screw terminal, 2 pins
  LED10 = LED - 3mm [color="Red (633nm)" package="3 mm [THT]"]

nets:
  GND: C25.0, IC6.pin3, R62.Pin_0, Q10.source, R72.Pin_1, R76.Pin_0, Q9.source, IC5.pin3, LED9.cathode, Q11.source, C24.0, LED13.cathode, R83.Pin_1, R86.Pin_1, Q12.source, R69.Pin_1, R80.Pin_0, LED14.cathode, R66.Pin_0, GND-5/12v.pin2, LED10.cathode
  5v/12v: C25.1, IC6.pin6, IC5.pin6, C24.1, GND-5/12v.pin1
  N1: IC6.pin2, R76.Pin_1, R73.Pin_1
  N2: IC6.pin4, R77.Pin_1, R80.Pin_1
  N3: IC6.pin5, R78.Pin_0
  N4: IC6.pin7, R74.Pin_1
  ING6-IN: R63.Pin_0, ING-IN.pin2
  N5: R63.Pin_1, IC5.pin4, R66.Pin_1
  N6: R62.Pin_1, IC5.pin2, R59.Pin_1
  12V: R84.Pin_0, R67.Pin_0, R70.Pin_0, R81.Pin_0
  N7: R84.Pin_1, LED16.anode
  N8: Q10.gate, R71.Pin_1
  INJ6-OUT: Q10.drain, D18.cathode, INJ-5/6-OUT.pin1
  N9: LED16.cathode, D20.anode
  INJ6-IN: R72.Pin_0, R71.Pin_0, INJ-IN.pin2
  N10: Q9.gate, R68.Pin_1
  INJ5-OUT: Q9.drain, D17.cathode, INJ-5/6-OUT.pin2
  N11: IC5.pin5, R64.Pin_0
  N12: IC5.pin7, R60.Pin_1
  N13: LED11.cathode, D17.anode
  N14: LED11.anode, R67.Pin_1
  INJ8-OUT: D20.cathode, Q12.drain, INJ-7/8-OUT.pin1
  ING8-IN: R77.Pin_0, ING-IN.pin4
  N15: LED15.cathode, D19.anode
  N16: LED15.anode, R81.Pin_1
  N17: LED9.anode, R61.Pin_0
  ING5-OUT: R60.Pin_0, R61.Pin_1, ING-5/6-OUT.pin2
  N18: R70.Pin_1, LED12.anode
  N19: Q11.gate, R82.Pin_1
  INJ7-OUT: Q11.drain, D19.cathode, INJ-7/8-OUT.pin2
  ING5-IN: R59.Pin_0, ING-IN.pin1
  N20: R65.Pin_0, LED10.anode
  ING6-OUT: R65.Pin_1, R64.Pin_1, ING-5/6-OUT.pin1
  ING7-IN: R73.Pin_0, ING-IN.pin3
  INJ7-IN: R82.Pin_0, R83.Pin_0, INJ-IN.pin3
  N21: LED13.anode, R75.Pin_0
  INJ5-IN: INJ-IN.pin1, R69.Pin_0, R68.Pin_0
  INJ8-IN: INJ-IN.pin4, R86.Pin_0, R85.Pin_0
  N22: LED12.cathode, D18.anode
  N23: Q12.gate, R85.Pin_1
  ING8-OUT: ING-7/8-OUT.pin1, R79.Pin_1, R78.Pin_1
  ING7-OUT: ING-7/8-OUT.pin2, R74.Pin_0, R75.Pin_1
  N24: R79.Pin_0, LED14.anode

notes:
  5
  6
  7
  8
  GND
  5V/12V
  INGNITOR
  Speeduino AddOn Ingition-Injector 5-6-7-8 Rev 0.1
